# Fritzing sketch circuit (saved by Fritzing 0.9.3b)
breadboards: 1

parts:
  U1 = Sharp Dust Sensor [part_number=GP2Y1010AU0F]
  F1 = Fan - Ventilador [package=THT]
  부품1 = Arduino Uno (Rev3) - ICSP
  C1 = Capacitor Polarized [package=cpol-radial-100uf-25v]
  R1 = Resistor [tolerance=±5% resistance=150 package="0402 [SMD]"]

nets:
  N1: U1.V-LED, C1.+, R1.Pin_1
  GND: U1.LED-GND, U1.S-GND, F1.GND, 부품1.GND, C1.-
  N2: U1.LED, 부품1.D2
  N3: U1.Vo, 부품1.A0
  VCC: U1.VCC, 부품1.5V, R1.Pin_0
  N4: F1.5V, 부품1.D13/SCK

custom parts:
  Sharp Dust Sensor: Sharp GP2Y1010AU0F Dust Sensor
  Fan - Ventilador: Ventilador de 2 pines, se encuentra comunmente en computadoras de escritorio
